# Fritzing sketch input (saved by Fritzing 0.9.2b)
breadboards: 1

parts:
  Raspberry_Pi1 = Raspberry Pi 2
  R1 = Resistor [tolerance=±5% resistance=100 package=THT]
  R2 = Resistor [tolerance=±5% resistance=10k package=THT]
  S2 = Pushbutton [package="[SMD]"]

nets:
  3V3: Raspberry_Pi1.3v3, Raspberry_Pi1.3V3, S2.Pin_3, S2.Pin_4
  N1: Raspberry_Pi1.GPIO7, R1.Pin_1
  N2: Raspberry_Pi1.GND, R2.Pin_1
  N3: R1.Pin_0, R2.Pin_0, S2.Pin_1, S2.Pin_2
