# Fritzing sketch input_output (saved by Fritzing 0.9.2b)
breadboards: 1

parts:
  Raspberry_Pi1 = Raspberry Pi 2
  R1 = Resistor [tolerance=±5% resistance=100 package=THT]
  R2 = Resistor [tolerance=±5% resistance=10k package=THT]
  S2 = Pushbutton [package="[SMD]"]
  LED1 = LED - 5mm [color="Red (633nm)" package="5 mm [THT]"]
  LED2 = LED - 5mm [color="Green (555nm)" package="5 mm [THT]"]
  R3 = Resistor [tolerance=±5% resistance=330 package=THT]
  R4 = Resistor [tolerance=±5% resistance=330 package=THT]

nets:
  3V3: Raspberry_Pi1.3v3, Raspberry_Pi1.5V, S2.Pin_3, S2.Pin_4
  N1: Raspberry_Pi1.GPIO7, R1.Pin_1
  N2: Raspberry_Pi1.GPIO8, R3.Pin_1
  N3: Raspberry_Pi1.GPIO25, R4.Pin_1
  N4: Raspberry_Pi1.GND, R2.Pin_1, LED1.cathode, LED2.cathode
  N5: R1.Pin_0, R2.Pin_0, S2.Pin_1, S2.Pin_2
  N6: LED1.anode, R4.Pin_0
  N7: LED2.anode, R3.Pin_0
